# Fritzing sketch SegmentChip (saved by Fritzing 0.9.0b)
circuit board: 5.7511cm x 4.40256cm
breadboards: 1

parts:
  Input = shrouded pin header, 10 pins [form="♂ (shrouded male)"]
  S1 = female pin header, 4 pins [form="♀ (female)"]
  S2 = female pin header, 4 pins [form="♀ (female)"]
  S3 = female pin header, 4 pins [form="♀ (female)"]
  S4 = female pin header, 4 pins [form="♀ (female)"]
  S5 = female pin header, 4 pins [form="♀ (female)"]
  S6 = female pin header, 4 pins [form="♀ (female)"]
  S7 = female pin header, 4 pins [form="♀ (female)"]

nets:
  N1: Input.pin1, S1.pin3, S2.pin3, S3.pin3, S4.pin3, S5.pin3, S6.pin3, S7.pin3
  N2: Input.pin2, S1.pin2, S2.pin2, S3.pin2, S4.pin2, S5.pin2, S6.pin2, S7.pin2
  N3: Input.pin3, S1.pin1
  N4: Input.pin4, S2.pin1
  N5: Input.pin5, S3.pin1
  N6: Input.pin6, S4.pin1
  N7: Input.pin7, S5.pin1
  N8: Input.pin8, S6.pin1
  N9: Input.pin9, S7.pin1
  N10: Input.pin10, S1.pin4, S2.pin4, S3.pin4, S4.pin4, S5.pin4, S6.pin4, S7.pin4
